// Logisim project proc_RAM.circ as structural Verilog: 1 circuit, main circuit main
module main (
);

  wire and_4_out, and_5_out, and_7_out, and_8_out, cdm_8_mark5_1_p1, cdm_8_mark5_1_p2, cdm_8_mark5_1_p4,
       cdm_8_mark5_1_p5, cdm_8_mark5_1_p6, cdm_8_mark5_1_p7, cdm_8_mark5_1_p8, Cl, code, comparator_1_eq,
       comparator_2_eq, comparator_3_eq, comparator_4_lt, comparator_5_gt, comparator_6_lt, comparator_7_gt,
       CORD_select, data, data_ins_prime, demultiplexer_1_out0, demultiplexer_1_out1, demultiplexer_1_out2,
       demultiplexer_1_out3, demultiplexer_1_out4, demultiplexer_1_out5, demultiplexer_1_out6,
       demultiplexer_1_out7, demultiplexer_1_out8, demultiplexer_1_out9, demultiplexer_1_out10,
       demultiplexer_1_out11, demultiplexer_1_out12, demultiplexer_1_out13, demultiplexer_1_out14,
       demultiplexer_1_out15, DISPLAY_select, DOWN_button, ENTER_out, hi, LEFT_button, lo, memory, not_1_out,
       not_2_out, not_3_out, not_4_out, not_7_out, or_1_out, or_2_out, or_3_out, or_4_out, read_write_prime,
       RIGHT_button, STOP_out, STOP_select, UP_button;
  wire [0:0] register_1_q, register_2_q;
  wire [3:0] column, Column_q, controlled_buffer_7_out, X_coord_q, Y_coord_q;
  wire [7:0] addr, cdm_8_mark5_1_p13, cdm_8_mark5_1_p14, D, ram_1_data, undriven;
  wire [15:0] register_3_q, register_4_q, register_5_q, register_6_q, register_7_q, register_8_q,
       register_9_q, register_10_q, register_11_q, register_12_q, register_13_q, register_14_q,
       register_15_q, register_16_q, register_17_q, register_18_q, row_value;

  // Debugger debugger_1: pin names not known
  // Probe on cdm_8_mark5_1_p5
  // Probe on cdm_8_mark5_1_p2
  // Probe on cdm_8_mark5_1_p1
  // Probe on cdm_8_mark5_1_p4
  Clock clock_1 (.out(Cl));
  Comparator comparator_1 (.a(addr), .b(8'hf2), .eq(comparator_1_eq));  // open: gt, lt
  Button UP (.out(UP_button));
  Button LEFT (.out(LEFT_button));
  Button DOWN (.out(DOWN_button));
  Comparator comparator_2 (.a(addr), .b(8'hf4), .eq(comparator_2_eq));  // open: gt, lt
  // Probe on cdm_8_mark5_1_p7
  // Probe on cdm_8_mark5_1_p6
  // Probe on cdm_8_mark5_1_p8
  // CdM_8_mark5 cdm_8_mark5_1: pin names not known; wires that end beside it: cdm_8_mark5_1_p1, cdm_8_mark5_1_p2, Cl, cdm_8_mark5_1_p4, cdm_8_mark5_1_p5, cdm_8_mark5_1_p6, cdm_8_mark5_1_p7, cdm_8_mark5_1_p8, data_ins_prime, memory, read_write_prime, addr, cdm_8_mark5_1_p13, cdm_8_mark5_1_p14
  Button RIGHT (.out(RIGHT_button));
  and and_1 (STOP_select, data_ins_prime, read_write_prime, comparator_1_eq);
  and and_2 (STOP_select, data_ins_prime, read_write_prime, comparator_2_eq);
  assign D = not_1_out ? cdm_8_mark5_1_p13 : 8'bz;  // Controlled_Buffer controlled_buffer_1
  not not_1 (not_1_out, read_write_prime);
  assign cdm_8_mark5_1_p14 = read_write_prime ? D : 8'bz;  // Controlled_Buffer controlled_buffer_2
  Button STOP (.out(STOP_out));
  Button ENTER (.out(ENTER_out));
  Decoder decoder_1 (.out0(code), .out1(data), .sel(data_ins_prime), .en(memory));
  not not_2 (not_2_out, register_2_q[0]);
  not not_3 (not_3_out, register_1_q[0]);
  Register #(.width(1)) register_1 (.D(not_3_out), .Q(register_1_q[0]), .clk(ENTER_out));  // open: en, clr
  Register #(.width(1)) register_2 (.D(not_2_out), .Q(register_2_q[0]), .clk(STOP_out));  // open: en, clr
  Counter #(.width(4), .max('hf)) X_coord (
    .load(LEFT_button), .count(or_1_out), .Q(X_coord_q), .clk(or_1_out));  // open: D, carry, clr
  or or_1 (or_1_out, RIGHT_button, LEFT_button);
  Counter #(.width(4), .max('hf)) Y_coord (
    .load(DOWN_button), .count(or_2_out), .Q(Y_coord_q), .clk(or_2_out));  // open: D, carry, clr
  or or_2 (or_2_out, UP_button, DOWN_button);
  assign D = STOP_select ? {{7{1'b0}}, register_1_q[0]} : 8'bz;  // Controlled_Buffer controlled_buffer_3
  ROM rom_1 (.addr(addr), .data(D), .sel(code));
  RAM ram_1 (.addr(addr), .data(ram_1_data), .sel(data), .clk(Cl), .ld(read_write_prime));  // open: clr
  or or_3 (or_3_out, STOP_select, CORD_select);
  assign D = STOP_select ? {{7{1'b0}}, register_2_q[0]} : 8'bz;  // Controlled_Buffer controlled_buffer_4
  Comparator comparator_3 (.a(addr), .b(8'hf3), .eq(comparator_3_eq));  // open: gt, lt
  assign ram_1_data = not_4_out ? D : 8'bz;  // Controlled_Buffer controlled_buffer_5
  not not_4 (not_4_out, or_3_out);
  assign D = CORD_select ? {Y_coord_q, X_coord_q} : 8'bz;  // Controlled_Buffer controlled_buffer_6
  and and_3 (CORD_select, data_ins_prime, read_write_prime, comparator_3_eq);
  assign {lo, column[3:1], controlled_buffer_7_out} = DISPLAY_select ? addr : 8'bz;  // Controlled_Buffer controlled_buffer_7
  Comparator comparator_4 (.a(addr), .b(8'hd0), .lt(comparator_4_lt));  // open: gt, eq
  Comparator comparator_5 (.a(addr), .b(8'haf), .gt(comparator_5_gt));  // open: eq, lt
  Comparator comparator_6 (.a(addr), .b(8'hf0), .lt(comparator_6_lt));  // open: gt, eq
  Comparator comparator_7 (.a(addr), .b(8'hcf), .gt(comparator_7_gt));  // open: eq, lt
  not not_5 (column[0], controlled_buffer_7_out[3]);
  and and_4 (and_4_out, comparator_4_lt, comparator_5_gt);
  and and_5 (and_5_out, comparator_6_lt, comparator_7_gt);
  not not_6 (hi, lo);
  or or_4 (or_4_out, and_4_out, and_5_out);
  not not_7 (not_7_out, read_write_prime);
  and and_6 (DISPLAY_select, or_4_out, data_ins_prime, not_7_out);
  and and_7 (and_7_out, DISPLAY_select, lo);
  and and_8 (and_8_out, DISPLAY_select, hi);
  assign D = DISPLAY_select ? undriven : 8'bz;  // Controlled_Buffer controlled_buffer_8
  Register #(.trigger("high")) u_lo (.D(undriven), .en(and_7_out), .Q(row_value[7:0]), .clk(and_7_out));  // open: clr
  Register #(.trigger("high")) u_hi (.D(undriven), .en(and_8_out), .Q(row_value[15:8]), .clk(and_8_out));  // open: clr
  Register #(.width(4)) u_Column (.D(column), .en(DISPLAY_select), .Q(Column_q), .clk(Cl));  // open: clr
  Demultiplexer #(.select(4)) demultiplexer_1 (
    .out0(demultiplexer_1_out0), .out1(demultiplexer_1_out1), .out2(demultiplexer_1_out2),
    .out3(demultiplexer_1_out3), .out4(demultiplexer_1_out4), .out5(demultiplexer_1_out5),
    .out6(demultiplexer_1_out6), .out7(demultiplexer_1_out7), .out8(demultiplexer_1_out8),
    .out9(demultiplexer_1_out9), .out10(demultiplexer_1_out10), .out11(demultiplexer_1_out11),
    .out12(demultiplexer_1_out12), .out13(demultiplexer_1_out13), .out14(demultiplexer_1_out14),
    .out15(demultiplexer_1_out15), .sel(Column_q), .en(DISPLAY_select));  // open: in
  Register #(.width(16)) register_3 (
    .D(row_value), .en(demultiplexer_1_out0), .Q(register_3_q), .clk(Cl));  // open: clr
  Register #(.width(16)) register_4 (
    .D(row_value), .en(demultiplexer_1_out1), .Q(register_4_q), .clk(Cl));  // open: clr
  Register #(.width(16)) register_5 (
    .D(row_value), .en(demultiplexer_1_out2), .Q(register_5_q), .clk(Cl));  // open: clr
  Register #(.width(16)) register_6 (
    .D(row_value), .en(demultiplexer_1_out3), .Q(register_6_q), .clk(Cl));  // open: clr
  Register #(.width(16)) register_7 (
    .D(row_value), .en(demultiplexer_1_out4), .Q(register_7_q), .clk(Cl));  // open: clr
  Register #(.width(16)) register_8 (
    .D(row_value), .en(demultiplexer_1_out5), .Q(register_8_q), .clk(Cl));  // open: clr
  Register #(.width(16)) register_9 (
    .D(row_value), .en(demultiplexer_1_out6), .Q(register_9_q), .clk(Cl));  // open: clr
  Register #(.width(16)) register_10 (
    .D(row_value), .en(demultiplexer_1_out7), .Q(register_10_q), .clk(Cl));  // open: clr
  Register #(.width(16)) register_11 (
    .D(row_value), .en(demultiplexer_1_out8), .Q(register_11_q), .clk(Cl));  // open: clr
  Register #(.width(16)) register_12 (
    .D(row_value), .en(demultiplexer_1_out9), .Q(register_12_q), .clk(Cl));  // open: clr
  Register #(.width(16)) register_13 (
    .D(row_value), .en(demultiplexer_1_out10), .Q(register_13_q), .clk(Cl));  // open: clr
  Register #(.width(16)) register_14 (
    .D(row_value), .en(demultiplexer_1_out11), .Q(register_14_q), .clk(Cl));  // open: clr
  Register #(.width(16)) register_15 (
    .D(row_value), .en(demultiplexer_1_out12), .Q(register_15_q), .clk(Cl));  // open: clr
  Register #(.width(16)) register_16 (
    .D(row_value), .en(demultiplexer_1_out13), .Q(register_16_q), .clk(Cl));  // open: clr
  Register #(.width(16)) register_17 (
    .D(row_value), .en(demultiplexer_1_out14), .Q(register_17_q), .clk(Cl));  // open: clr
  Register #(.width(16)) register_18 (
    .D(row_value), .en(demultiplexer_1_out15), .Q(register_18_q), .clk(Cl));  // open: clr
  DotMatrix #(.matrixcols(16), .matrixrows(16)) dotmatrix_1 (
    .col0(register_3_q), .col1(register_4_q), .col2(register_5_q), .col3(register_6_q), .col4(register_7_q),
    .col5(register_8_q), .col6(register_9_q), .col7(register_10_q), .col8(register_11_q),
    .col9(register_12_q), .col10(register_13_q), .col11(register_14_q), .col12(register_15_q),
    .col13(register_16_q), .col14(register_17_q), .col15(register_18_q));

  // Notes on the sheet:
  //   contents of rom_1 (hex, n*v repeats v):
  //   d0 b0 88 c1 d1 9 a4 c5 cd 0 d0 0 8c d1 c0 a4 8d 89 a4 d4
endmodule
